// Logisim project PIPO.circ as structural Verilog: 1 circuit, main circuit main
module main (
  input  D_0,
  input  D_1,
  input  D_2,
  input  D_3
);

  wire clock_1_out, d_ff_1_q, d_ff_2_q, d_ff_3_q, d_ff_4_q;

  Clock clock_1 (.out(clock_1_out));
  LED L_0 (.in(d_ff_1_q));
  D_Flip_Flop d_ff_1 (.clk(clock_1_out), .D(D_0), .Q(d_ff_1_q));  // open: Qn, preset, en, reset
  LED L_1 (.in(d_ff_2_q));
  D_Flip_Flop d_ff_2 (.clk(clock_1_out), .D(D_1), .Q(d_ff_2_q));  // open: Qn, preset, en, reset
  D_Flip_Flop d_ff_3 (.clk(clock_1_out), .D(D_2), .Q(d_ff_3_q));  // open: Qn, preset, en, reset
  LED L_2 (.in(d_ff_3_q));
  LED L_3 (.in(d_ff_4_q));
  D_Flip_Flop d_ff_4 (.clk(clock_1_out), .D(D_3), .Q(d_ff_4_q));  // open: Qn, preset, en, reset
endmodule
