// Logisim project SIPO.circ as structural Verilog: 1 circuit, main circuit main
module main (
  input  In
);

  wire clock_1_out, D0_q, D1_q, D2_q, D3_q;

  Clock clock_1 (.out(clock_1_out));
  D_Flip_Flop D0 (.clk(clock_1_out), .D(In), .Q(D0_q));  // open: Qn, preset, en, reset
  LED L0 (.in(D0_q));
  LED L1 (.in(D1_q));
  D_Flip_Flop D1 (.clk(clock_1_out), .D(D0_q), .Q(D1_q));  // open: Qn, preset, en, reset
  LED L_2 (.in(D2_q));
  D_Flip_Flop D2 (.clk(clock_1_out), .D(D1_q), .Q(D2_q));  // open: Qn, preset, en, reset
  LED L_3 (.in(D3_q));
  D_Flip_Flop D3 (.clk(clock_1_out), .D(D2_q), .Q(D3_q));  // open: Qn, preset, en, reset
endmodule
