// Logisim project demo circuit 4.circ as structural Verilog: 3 circuits, main circuit main
module main (
  input  in_1,
  input  in_2,
  input  in_3,
  output out_4
);

  wire and_1_out, and_2_out, and_3_out, nand_1_out, not_1_out, not_2_out;

  not not_1 (not_1_out, in_1);
  not not_2 (not_2_out, in_3);
  and and_1 (and_1_out, not_1_out, in_2);
  and and_2 (and_2_out, not_1_out, in_2, in_3);
  and and_3 (and_3_out, in_1, in_2, not_2_out);
  nand nand_1 (nand_1_out, in_1, in_2, in_3);
  or or_1 (out_4, and_1_out, and_2_out, and_3_out, nand_1_out);
endmodule

module Basic_cir (
  input  x,
  input  y,
  input  z,
  output q
);

  wire nand_1_out, nand_2_out, nand_3_out, nand_4_out, nand_5_out, nand_6_out, nand_7_out, nand_8_out,
       nand_9_out, nand_10_out, nand_11_out, nand_12_out, nand_13_out, nand_14_out, nand_15_out, nand_16_out,
       nand_17_out, nand_18_out;

  nand nand_1 (nand_1_out, x, x);
  nand nand_2 (nand_2_out, x, y);
  nand nand_3 (nand_3_out, nand_1_out, y);
  nand nand_4 (nand_4_out, x, y);
  nand nand_5 (nand_5_out, nand_2_out, nand_2_out);
  nand nand_6 (nand_6_out, x, x);
  nand nand_7 (nand_7_out, nand_3_out, nand_3_out);
  nand nand_8 (nand_8_out, nand_4_out, nand_4_out);
  nand nand_9 (nand_9_out, z, z);
  nand nand_10 (nand_10_out, nand_5_out, z);
  nand nand_11 (nand_11_out, nand_6_out, y);
  nand nand_12 (nand_12_out, nand_7_out, z);
  nand nand_13 (nand_13_out, nand_8_out, nand_9_out);
  nand nand_14 (nand_14_out, nand_10_out, nand_10_out);
  nand nand_15 (nand_15_out, nand_11_out, nand_12_out);
  nand nand_16 (nand_16_out, nand_13_out, nand_14_out);
  nand nand_17 (nand_17_out, nand_15_out, nand_15_out);
  nand nand_18 (nand_18_out, nand_16_out, nand_16_out);
  nand nand_19 (q, nand_17_out, nand_18_out);
endmodule

module basic (
  input  x,
  input  y,
  input  z,
  output q
);

  wire not_1_out, not_2_out, not_3_out, or_1_out;

  not not_1 (not_1_out, x);
  not not_2 (not_2_out, y);
  or or_1 (or_1_out, not_1_out, not_2_out);
  not not_3 (not_3_out, z);
  or or_2 (q, or_1_out, not_3_out);
endmodule
