// Logisim project demo circuit-1.circ as structural Verilog: 1 circuit, main circuit main
module main (
  input  A,
  input  B,
  input  C,
  output Y
);

  wire and_1_out, and_2_out, and_3_out, not_1_out, or_1_out;

  not not_1 (not_1_out, B);
  and and_1 (and_1_out, A, B);
  or or_1 (or_1_out, A, not_1_out);
  and and_2 (and_2_out, and_1_out, or_1_out);
  and and_3 (and_3_out, A, C);
  or or_2 (Y, and_2_out, and_3_out);
endmodule
