// Logisim project down counter.circ as structural Verilog: 1 circuit, main circuit main
module main (
  input  In,
  output Qc,
  output Qb,
  output Qa
);

  wire clock_1_out;

  Clock clock_1 (.out(clock_1_out));
  J_K_Flip_Flop j_k_ff_1 (.J(In), .clk(clock_1_out), .K(In), .Q(Qa));  // open: Qn, preset, en, reset
  J_K_Flip_Flop j_k_ff_2 (.J(In), .clk(Qa), .K(In), .Q(Qb));  // open: Qn, preset, en, reset
  J_K_Flip_Flop j_k_ff_3 (.J(In), .clk(Qb), .K(In), .Q(Qc));  // open: Qn, preset, en, reset
endmodule
