// Logisim project jk ff.circ as structural Verilog: 1 circuit, main circuit main
module main (
  input  J,
  input  K,
  output Q,
  output Q_prime
);

  wire CLK_out;

  Clock CLK (.out(CLK_out));
  J_K_Flip_Flop J_K (.J(J), .clk(CLK_out), .K(K), .Q(Q), .Qn(Q_prime));  // open: preset, en, reset
endmodule
