// Logisim project sr flip flop.circ as structural Verilog: 1 circuit, main circuit main
module main (
  input  in_1,
  input  in_2,
  output out_3,
  output out_4
);

  wire clock_1_out;

  Clock clock_1 (.out(clock_1_out));
  S_R_Flip_Flop s_r_ff_1 (.S(in_1), .clk(clock_1_out), .R(in_2), .Q(out_3), .Qn(out_4));  // open: preset, reset, en
endmodule
