// Logisim project up counter.circ as structural Verilog: 1 circuit, main circuit main
module main (
  input  in_1,
  output Qc,
  output Qb,
  output Qa
);

  wire clock_1_out, j_k_ff_1_q, j_k_ff_2_q;

  Clock clock_1 (.out(clock_1_out));
  J_K_Flip_Flop j_k_ff_1 (.J(in_1), .clk(clock_1_out), .K(in_1), .Q(j_k_ff_1_q), .Qn(Qa));  // open: preset, en, reset
  J_K_Flip_Flop j_k_ff_2 (.J(in_1), .clk(j_k_ff_1_q), .K(in_1), .Q(j_k_ff_2_q), .Qn(Qb));  // open: preset, en, reset
  J_K_Flip_Flop j_k_ff_3 (.J(in_1), .clk(j_k_ff_2_q), .K(in_1), .Qn(Qc));  // open: Q, preset, en, reset
endmodule
