// Logisim project up down counter.circ as structural Verilog: 1 circuit, main circuit main
module main (
  input  M,
  input  in_2,
  output Qc,
  output Qb,
  output Qa
);

  wire and_1_out, and_2_out, and_3_out, and_4_out, clock_1_out, j_k_ff_1_qn, j_k_ff_2_qn, not_1_out,
       or_1_out, or_2_out;

  Clock clock_1 (.out(clock_1_out));
  not not_1 (not_1_out, M);
  J_K_Flip_Flop j_k_ff_1 (.J(in_2), .clk(clock_1_out), .K(in_2), .Q(Qa), .Qn(j_k_ff_1_qn));  // open: preset, en, reset
  and and_1 (and_1_out, not_1_out, Qa);
  and and_2 (and_2_out, M, j_k_ff_1_qn);
  or or_1 (or_1_out, and_1_out, and_2_out);
  J_K_Flip_Flop j_k_ff_2 (.J(in_2), .clk(or_1_out), .K(in_2), .Q(Qb), .Qn(j_k_ff_2_qn));  // open: preset, en, reset
  and and_3 (and_3_out, not_1_out, Qb);
  and and_4 (and_4_out, M, j_k_ff_2_qn);
  or or_2 (or_2_out, and_3_out, and_4_out);
  J_K_Flip_Flop j_k_ff_3 (.J(in_2), .clk(or_2_out), .K(in_2), .Q(Qc));  // open: Qn, preset, en, reset
endmodule
